// Digital circuit Lab02.dig as structural Verilog
module Lab02 (
  input  B,
  input  C,
  input  A,
  input  D,
  output Fa,
  output Fb,
  output Fc,
  output Fd,
  output Fe,
  output Fg,
  output Ff
);

  wire A_t, and_1_out, and_2_out, and_3_out, and_4_out, and_5_out, and_6_out, B_t, C_t, D_t;

  and and_1 (and_1_out, B_t, D_t);
  and and_2 (and_2_out, A_t, C);
  and and_3 (and_3_out, A_t, B, D);
  and and_4 (and_4_out, A, B, C);
  and and_5 (and_5_out, A, B_t, C_t);
  and and_6 (and_6_out, A, C, D_t);
  or or_1 (Fa, and_1_out, and_2_out, and_3_out, and_4_out, and_5_out, and_6_out);
  not not_1 (A_t, A);
  not not_2 (B_t, B);
  not not_3 (C_t, C);
  not not_4 (D_t, D);
endmodule
